# Fritzing sketch BB-Arduino-Shift-Register-7-segment-clock (saved by Fritzing 0.8.7b)
circuit board: 5.55978cm x 2.65717cm
breadboards: 1

parts:
  U1 = Voltage Regulator - 5V [package="TO220 [THT]"]
  Power_plug1 = Power plug
  J5 = female pin header, 14 pins [form="♀ (female rounded)"]
  S2 = Pushbutton [package="[THT]"]
  C2 = Electrolytic Capacitor [capacitance=10µF rated_voltage=35V package="100 mil [THT, electrolytic]"]
  C1 = Electrolytic Capacitor [capacitance=10µF rated_voltage=35V package="100 mil [THT, electrolytic]"]
  C6 = Ceramic Capacitor [capacitance=22pF rated_voltage=35V package="200 mil [THT, multilayer]"]
  C5 = Ceramic Capacitor [capacitance=22pF rated_voltage=35V package="200 mil [THT, multilayer]"]
  XTAL1 = Crystal [frequency="16 Mhz" package=THT]
  R2 = Resistor [tolerance=±5% resistance=1k package=THT]
  J4 = female pin header, 14 pins [form="♀ (female rounded)"]
  U3 = 74HC595 [package="DIP16 [THT]"]
  U4 = 74HC595 [package="DIP16 [THT]"]
  part = 74HC595 [package="DIP16 [THT]"]  # not connected
  U2 = atmega168 [package=dip]

nets:
  N1: U1.input_voltage, Power_plug1.VCC, C1.+
  GND: U1.GND, Power_plug1.GND, J5.pin8, S2.Pin_3, S2.Pin_4, C2.-, C1.-, C6.0, C5.1, J4.pin7, U3.GND, U4.GND, U2.GND
  VCC: U1.output_voltage, J5.pin7, C2.+, R2.Pin_0, J4.pin8, J4.pin9, U3.VCC, U4.VCC, U2.VCC, U2.AVCC, U2.AREF
  N2: J5.pin1, S2.Pin_1, S2.Pin_2, R2.Pin_1, U2.RESET
  N3: J5.pin2, U2.D0_(RX)
  N4: J5.pin3, U2.D1_(TX)
  N5: J5.pin4, U2.D2
  N6: J5.pin5, U2.D3_(PWM)
  N7: J5.pin6, U2.D4
  N8: J5.pin9, C6.1, XTAL1.pin_0, U2.XLAT1
  N9: J5.pin10, C5.0, XTAL1.pin_1, U2.XLAT2
  N10: J5.pin11, U2.D5_(PWM)
  N11: J5.pin12, U2.D6_(PWM)
  N12: J5.pin13, U2.D7
  N13: J5.pin14, U2.D8
  N14: J4.pin1, U2.A5
  N15: J4.pin2, U2.A4
  N16: J4.pin3, U2.A3
  N17: J4.pin4, U2.A2
  N18: J4.pin5, U2.A1
  N19: J4.pin6, U2.A0
  N20: J4.pin10, U2.D13
  N21: J4.pin11, U2.D12
  N22: J4.pin12, U2.D11_(PWM)
  N23: J4.pin13, U2.D10_(PWM)
  N24: J4.pin14, U2.D9_(PWM)

notes:
  This is a breadboard Arduino without an FTDI chip. You can program the chip with a USB-Serial breakout board, by using an external programmer or by programming the MCU in an Arduino board and then popping it into this circuit. The power source should be at least 7 VDC. Related example: http://itp.nyu.edu/physcomp/Tutorials/ArduinoBreadboard
