# Fritzing sketch Barebone_Arduino-no-FTDI (saved by Fritzing 0.8.7b)
breadboards: 1

parts:
  C6 = Electrolytic Capacitor [capacitance=1µF package="100 mil [THT, electrolytic]"]
  C7 = Electrolytic Capacitor [capacitance=1µF package="100 mil [THT, electrolytic]"]
  U3 = Voltage Regulator - 5V [package="TO220 [THT]"]
  U4 = atmega168 [package=dip]
  XTAL2 = Crystal [frequency="16 Mhz" package=THT]
  S2 = Pushbutton [package="[THT]"]
  Power_plug2 = Power plug
  R2 = Resistor [tolerance=±5% resistance=1k package=THT]
  C8 = Ceramic Capacitor [capacitance=100nF package="200 mil [THT, multilayer]"]
  C5 = Ceramic Capacitor [capacitance=100nF package="200 mil [THT, multilayer]"]

nets:
  GND: C6.-, C7.-, U3.GND, U4.GND#21, Power_plug2.GND
  N1: C6.+, U3.input_voltage, Power_plug2.VCC
  N2: C7.+, U3.output_voltage, U4.VCC, U4.AVCC, U4.AREF, R2.Pin_0
  N3: U4.RESET, S2.Pin_1, S2.Pin_2, R2.Pin_1
  N4: U4.GND#7, S2.Pin_3, S2.Pin_4, C8.0, C5.1
  N5: U4.XLAT1, XTAL2.pin_0, C8.1
  N6: U4.XLAT2, XTAL2.pin_1, C5.0
