# Fritzing sketch Pomodoro_Nano_Matrix_RTC (saved by Fritzing 0.8.7b)
breadboards: 1

parts:
  Part4 = Real Time Clock Module - DS1307 RTC Breakout Board
  Part5 = Arduino Nano (Rev3.0)
  LED5 = LED - 3mm [color="Green (570nm)" package="3 mm [THT]"]
  LED6 = LED - 3mm [color="Red (633nm)" package="3 mm [THT]"]
  R2 = Resistor [tolerance=±5% resistance=220 package=THT]
  S2 = Pushbutton [package="[THT]"]

nets:
  5V: Part4.5V, Part5.5V, R2.Pin_0, S2.Pin_1, S2.Pin_2
  GND: Part4.GND, Part5.GND, R2.Pin_1
  N1: Part4.SCL, Part5.A5
  N2: Part4.SDA, Part5.A4
  N3: Part5.D8, LED5.cathode
  N4: Part5.D9, LED6.cathode
  N5: LED5.anode, LED6.anode
  N6: S2.Pin_3, S2.Pin_4
